// Logisim project 4BIT_COMPUTING_DEVICE.circ as structural Verilog: 1 circuit, main circuit main
module main (
  input  [3:0] in_1,
  input  [3:0] in_2,
  input  [3:0] in_3,
  input  [7:0] in_4,
  input  [7:0] in_5,
  output [3:0] out_6,
  output [3:0] out_7,
  output [3:0] out_8,
  output [3:0] out_9,
  output [3:0] out_10,
  output [3:0] out_11,
  output [3:0] out_12
);

  wire main_4_out_11, main_4_out_12, main_4_out_13, main_4_out_14, main_7_out_11, main_7_out_12,
       main_7_out_13, main_7_out_14, main_8_out_11, main_8_out_12, main_8_out_13, main_8_out_14,
       main_9_out_11, main_9_out_12, main_9_out_13, main_9_out_14, main_10_out_11, main_10_out_12,
       main_10_out_13, main_10_out_14, main_11_out_11, main_11_out_12, main_11_out_13, main_11_out_14,
       main_12_out_11, main_12_out_12, main_12_out_13, main_12_out_14, main_13_out_11, main_13_out_12,
       main_13_out_13, main_13_out_14, main_14_out_11, main_14_out_12, main_14_out_13, main_14_out_14,
       main_15_out_11, main_15_out_12, main_15_out_13, main_15_out_14, main_18_out_13, main_18_out_14,
       main_18_out_15, main_18_out_16, main_20_out_11, main_20_out_12, main_20_out_13, main_20_out_14,
       main_24_out_11, main_24_out_12, main_24_out_13, main_24_out_14, main_25_out_11, main_25_out_12,
       main_25_out_13, main_25_out_14, main_26_out_11, main_26_out_12, main_26_out_13, main_26_out_14,
       main_27_out_11, main_27_out_12, main_27_out_13, main_27_out_14, main_28_out_11, main_28_out_12,
       main_28_out_13, main_28_out_14, main_29_out_11, main_29_out_12, main_29_out_13, main_29_out_14,
       main_30_out_11, main_30_out_12, main_30_out_13, main_30_out_14, main_31_out_11, main_31_out_12,
       main_31_out_13, main_31_out_14, main_35_out_11, main_35_out_12, main_35_out_13, main_35_out_14;

  DIODE_main main_1 (.in_1(main_4_out_11), .out_2(out_11[0]));
  DIODE_main main_2 (.in_1(main_4_out_12), .out_2(out_11[1]));
  DIODE_main main_3 (.in_1(main_4_out_13), .out_2(out_11[3]));
  _7408_AND_main main_4 (
    .in_2(in_4[2]), .in_3(in_3[0]), .out_11(main_4_out_11), .in_4(in_4[2]), .in_5(in_3[1]),
    .out_12(main_4_out_12), .in_6(in_4[2]), .in_7(in_3[3]), .out_13(main_4_out_13), .in_8(in_4[2]),
    .in_9(in_3[2]), .out_14(main_4_out_14));  // open: GND, Vcc
  _7408_AND_main main_5 (
    .in_2(in_4[1]), .in_3(in_3[0]), .out_11(out_8[0]), .in_4(in_4[1]), .in_5(in_3[1]), .out_12(out_8[1]),
    .in_6(in_4[1]), .in_7(in_3[3]), .out_13(out_8[3]), .in_8(in_4[1]), .in_9(in_3[2]), .out_14(out_8[2]));  // open: GND, Vcc
  DIODE_main main_6 (.in_1(main_4_out_14), .out_2(out_11[2]));
  _7408_AND_main main_7 (
    .in_2(in_3[0]), .in_3(main_7_out_12), .out_11(main_7_out_11), .in_4(in_3[1]), .in_5(main_7_out_14),
    .out_12(main_7_out_12), .in_6(1'b1), .in_7(in_3[3]), .out_13(main_7_out_13), .in_8(main_7_out_13),
    .in_9(in_3[2]), .out_14(main_7_out_14));  // open: GND, Vcc
  _7432_OR_main main_8 (
    .in_2(in_3[0]), .in_3(in_2[0]), .out_11(main_8_out_11), .in_4(in_3[1]), .in_5(in_2[1]),
    .out_12(main_8_out_12), .in_6(in_3[3]), .in_7(in_2[3]), .out_13(main_8_out_13), .in_8(in_3[2]),
    .in_9(in_2[2]), .out_14(main_8_out_14));  // open: GND, Vcc
  _7432_OR_main main_9 (
    .in_2(in_1[0]), .in_3(in_3[0]), .out_11(main_9_out_11), .in_4(in_1[1]), .in_5(in_3[1]),
    .out_12(main_9_out_12), .in_6(in_1[3]), .in_7(in_3[3]), .out_13(main_9_out_13), .in_8(in_1[2]),
    .in_9(in_3[2]), .out_14(main_9_out_14));  // open: GND, Vcc
  _7432_OR_main main_10 (
    .in_2(in_1[0]), .in_3(in_2[0]), .out_11(main_10_out_11), .in_4(in_1[1]), .in_5(in_2[1]),
    .out_12(main_10_out_12), .in_6(in_1[3]), .in_7(in_2[3]), .out_13(main_10_out_13), .in_8(in_1[2]),
    .in_9(in_2[2]), .out_14(main_10_out_14));  // open: GND, Vcc
  _7432_OR_main main_11 (
    .in_2(in_1[0]), .in_3(in_2[0]), .out_11(main_11_out_11), .in_4(in_1[1]), .in_5(in_2[1]),
    .out_12(main_11_out_12), .in_6(in_1[3]), .in_7(in_2[3]), .out_13(main_11_out_13), .in_8(in_1[2]),
    .in_9(in_2[2]), .out_14(main_11_out_14));  // open: GND, Vcc
  _7486_XOR_main main_12 (
    .in_2(in_1[0]), .in_3(in_2[0]), .out_11(main_12_out_11), .in_4(in_1[1]), .in_5(in_2[1]),
    .out_12(main_12_out_12), .in_6(in_1[3]), .in_7(in_2[3]), .out_13(main_12_out_13), .in_8(in_1[2]),
    .in_9(in_2[2]), .out_14(main_12_out_14));  // open: GND, Vcc
  _7402_NOR_main main_13 (
    .in_3(in_1[0]), .in_2(in_2[0]), .out_11(main_13_out_11), .in_5(in_2[1]), .in_4(in_1[1]),
    .out_12(main_13_out_12), .in_7(in_1[3]), .in_6(in_2[3]), .out_13(main_13_out_13), .GND(in_1[2]),
    .in_8(in_2[2]), .out_14(main_13_out_14));  // open: in_10, Vcc
  _7432_OR_main main_14 (
    .in_2(in_1[0]), .in_3(in_2[0]), .out_11(main_14_out_11), .in_4(in_1[1]), .in_5(in_2[1]),
    .out_12(main_14_out_12), .in_6(in_1[3]), .in_7(in_2[3]), .out_13(main_14_out_13), .in_8(in_1[2]),
    .in_9(in_2[2]), .out_14(main_14_out_14));  // open: GND, Vcc
  _7408_AND_main main_15 (
    .in_2(in_1[0]), .in_3(in_2[0]), .out_11(main_15_out_11), .in_4(in_1[1]), .in_5(in_2[1]),
    .out_12(main_15_out_12), .in_6(in_1[3]), .in_7(in_2[3]), .out_13(main_15_out_13), .in_8(in_1[2]),
    .in_9(in_2[2]), .out_14(main_15_out_14));  // open: GND, Vcc
  DIODE_main main_16 (.in_1(main_20_out_11), .out_2(out_10[0]));
  DIODE_main main_17 (.in_1(main_20_out_13), .out_2(out_10[3]));
  _74157_QUAD_BIT_SELECTOR_main main_18 (
    .in_7(main_7_out_11), .in_8(in_1[3]), .out_15(main_18_out_15), .in_9(in_2[3]), .in_10(in_1[2]),
    .out_16(main_18_out_16), .in_3(in_1[0]), .in_4(in_2[0]), .out_13(main_18_out_13), .in_5(in_1[1]),
    .in_6(in_2[1]), .out_14(main_18_out_14), .in_11(in_2[2]));  // open: GND, Vcc, G
  DIODE_main main_19 (.in_1(main_20_out_12), .out_2(out_10[1]));
  _7408_AND_main main_20 (
    .in_2(in_4[2]), .in_3(in_2[0]), .out_11(main_20_out_11), .in_4(in_4[2]), .in_5(in_2[1]),
    .out_12(main_20_out_12), .in_6(in_4[2]), .in_7(in_2[3]), .out_13(main_20_out_13), .in_8(in_4[2]),
    .in_9(in_2[2]), .out_14(main_20_out_14));  // open: GND, Vcc
  _7408_AND_main main_21 (
    .in_2(in_4[1]), .in_3(in_2[0]), .out_11(out_7[0]), .in_4(in_4[1]), .in_5(in_2[1]), .out_12(out_7[1]),
    .in_6(in_4[1]), .in_7(in_2[3]), .out_13(out_7[3]), .in_8(in_4[1]), .in_9(in_2[2]), .out_14(out_7[2]));  // open: GND, Vcc
  DIODE_main main_22 (.in_1(main_20_out_14), .out_2(out_10[2]));
  _7408_AND_main main_23 (
    .in_2(main_18_out_13), .in_3(in_4[0]), .out_11(out_12[0]), .in_4(main_18_out_14), .in_5(in_4[0]),
    .out_12(out_12[1]), .in_6(in_4[0]), .in_7(main_18_out_15), .out_13(out_12[3]), .in_8(in_4[0]),
    .in_9(main_18_out_16), .out_14(out_12[2]));  // open: GND, Vcc
  _7408_AND_main main_24 (
    .in_2(main_8_out_11), .in_3(in_5[7]), .out_11(main_24_out_11), .in_4(main_8_out_12), .in_5(in_5[7]),
    .out_12(main_24_out_12), .in_6(main_8_out_13), .in_7(in_5[7]), .out_13(main_24_out_13),
    .in_8(main_8_out_14), .in_9(in_5[7]), .out_14(main_24_out_14));  // open: GND, Vcc
  _7408_AND_main main_25 (
    .in_2(main_9_out_11), .in_3(in_5[6]), .out_11(main_25_out_11), .in_4(main_9_out_12), .in_5(in_5[6]),
    .out_12(main_25_out_12), .in_6(main_9_out_13), .in_7(in_5[6]), .out_13(main_25_out_13),
    .in_8(main_9_out_14), .in_9(in_5[6]), .out_14(main_25_out_14));  // open: GND, Vcc
  _7408_AND_main main_26 (
    .in_2(main_10_out_11), .in_3(in_5[5]), .out_11(main_26_out_11), .in_4(main_10_out_12), .in_5(in_5[5]),
    .out_12(main_26_out_12), .in_6(main_10_out_13), .in_7(in_5[5]), .out_13(main_26_out_13),
    .in_8(main_10_out_14), .in_9(in_5[5]), .out_14(main_26_out_14));  // open: GND, Vcc
  _7408_AND_main main_27 (
    .in_2(main_11_out_11), .in_3(in_5[4]), .out_11(main_27_out_11), .in_4(main_11_out_12), .in_5(in_5[4]),
    .out_12(main_27_out_12), .in_6(main_11_out_13), .in_7(in_5[4]), .out_13(main_27_out_13),
    .in_8(main_11_out_14), .in_9(in_5[4]), .out_14(main_27_out_14));  // open: GND, Vcc
  _7408_AND_main main_28 (
    .in_2(main_12_out_11), .in_3(in_5[3]), .out_11(main_28_out_11), .in_4(main_12_out_12), .in_5(in_5[3]),
    .out_12(main_28_out_12), .in_6(main_12_out_13), .in_7(in_5[3]), .out_13(main_28_out_13),
    .in_8(main_12_out_14), .in_9(in_5[3]), .out_14(main_28_out_14));  // open: GND, Vcc
  _7408_AND_main main_29 (
    .in_2(main_13_out_11), .in_3(in_5[2]), .out_11(main_29_out_11), .in_4(main_13_out_12), .in_5(in_5[2]),
    .out_12(main_29_out_12), .in_6(main_13_out_13), .in_7(in_5[2]), .out_13(main_29_out_13),
    .in_8(main_13_out_14), .in_9(in_5[2]), .out_14(main_29_out_14));  // open: GND, Vcc
  _7408_AND_main main_30 (
    .in_2(main_14_out_11), .in_3(in_5[1]), .out_11(main_30_out_11), .in_4(main_14_out_12), .in_5(in_5[1]),
    .out_12(main_30_out_12), .in_6(main_14_out_13), .in_7(in_5[1]), .out_13(main_30_out_13),
    .in_8(main_14_out_14), .in_9(in_5[1]), .out_14(main_30_out_14));  // open: GND, Vcc
  _7408_AND_main main_31 (
    .in_2(main_15_out_11), .in_3(in_5[0]), .out_11(main_31_out_11), .in_4(main_15_out_12), .in_5(in_5[0]),
    .out_12(main_31_out_12), .in_6(main_15_out_13), .in_7(in_5[0]), .out_13(main_31_out_13),
    .in_8(main_15_out_14), .in_9(in_5[0]), .out_14(main_31_out_14));  // open: GND, Vcc
  DIODE_main main_32 (.in_1(main_35_out_11), .out_2(out_9[0]));
  DIODE_main main_33 (.in_1(main_35_out_12), .out_2(out_9[1]));
  DIODE_main main_34 (.in_1(main_35_out_13), .out_2(out_9[3]));
  _7408_AND_main main_35 (
    .in_2(in_4[2]), .in_3(in_1[0]), .out_11(main_35_out_11), .in_4(in_4[2]), .in_5(in_1[1]),
    .out_12(main_35_out_12), .in_6(in_4[2]), .in_7(in_1[3]), .out_13(main_35_out_13), .in_8(in_4[2]),
    .in_9(in_1[2]), .out_14(main_35_out_14));  // open: GND, Vcc
  _7408_AND_main main_36 (
    .in_2(in_4[1]), .in_3(in_1[0]), .out_11(out_6[0]), .in_4(in_4[1]), .in_5(in_1[1]), .out_12(out_6[1]),
    .in_6(in_4[1]), .in_7(in_1[3]), .out_13(out_6[3]), .in_8(in_4[1]), .in_9(in_1[2]), .out_14(out_6[2]));  // open: GND, Vcc
  DIODE_main main_37 (.in_1(main_35_out_14), .out_2(out_9[2]));
  DIODE_main main_38 (.in_1(main_24_out_11), .out_2(out_9[0]));
  DIODE_main main_39 (.in_1(main_24_out_12), .out_2(out_9[1]));
  DIODE_main main_40 (.in_1(main_24_out_14), .out_2(out_9[2]));
  DIODE_main main_41 (.in_1(main_24_out_13), .out_2(out_9[3]));
  DIODE_main main_42 (.in_1(main_25_out_11), .out_2(out_10[0]));
  DIODE_main main_43 (.in_1(main_25_out_12), .out_2(out_10[1]));
  DIODE_main main_44 (.in_1(main_25_out_14), .out_2(out_10[2]));
  DIODE_main main_45 (.in_1(main_25_out_13), .out_2(out_10[3]));
  DIODE_main main_46 (.in_1(main_26_out_11));  // open: out_2
  DIODE_main main_47 (.in_1(main_26_out_12), .out_2(out_11[0]));
  DIODE_main main_48 (.in_1(main_26_out_14), .out_2(out_11[1]));
  DIODE_main main_49 (.in_1(main_26_out_13), .out_2(out_11[2]));
  DIODE_main main_50 (.in_1(main_27_out_11), .out_2(out_11[1]));
  DIODE_main main_51 (.in_1(main_27_out_12), .out_2(out_11[2]));
  DIODE_main main_52 (.in_1(main_27_out_14), .out_2(out_11[3]));
  DIODE_main main_53 (.in_1(main_27_out_13));  // open: out_2
  DIODE_main main_54 (.in_1(main_28_out_11), .out_2(out_11[0]));
  DIODE_main main_55 (.in_1(main_28_out_12), .out_2(out_11[1]));
  DIODE_main main_56 (.in_1(main_28_out_14), .out_2(out_11[2]));
  DIODE_main main_57 (.in_1(main_28_out_13), .out_2(out_11[3]));
  DIODE_main main_58 (.in_1(main_29_out_11), .out_2(out_11[0]));
  DIODE_main main_59 (.in_1(main_29_out_12), .out_2(out_11[1]));
  DIODE_main main_60 (.in_1(main_29_out_14), .out_2(out_11[2]));
  DIODE_main main_61 (.in_1(main_29_out_13), .out_2(out_11[3]));
  DIODE_main main_62 (.in_1(main_30_out_11), .out_2(out_11[0]));
  DIODE_main main_63 (.in_1(main_30_out_12), .out_2(out_11[1]));
  DIODE_main main_64 (.in_1(main_30_out_14), .out_2(out_11[2]));
  DIODE_main main_65 (.in_1(main_30_out_13), .out_2(out_11[3]));
  DIODE_main main_66 (.in_1(main_31_out_11), .out_2(out_11[0]));
  DIODE_main main_67 (.in_1(main_31_out_12), .out_2(out_11[1]));
  DIODE_main main_68 (.in_1(main_31_out_14), .out_2(out_11[2]));
  DIODE_main main_69 (.in_1(main_31_out_13), .out_2(out_11[3]));
endmodule
