// Logisim project 7400 NAND.circ as structural Verilog: 1 circuit, main circuit main
module main (
  input  Vcc,
  input  in_2,
  input  in_3,
  input  in_4,
  input  in_5,
  input  in_6,
  input  in_7,
  input  in_8,
  input  in_9,
  input  GND,
  output out_11,
  output out_12,
  output out_13,
  output out_14
);

  nand nand_1 (out_13, in_6, in_7);
  nand nand_2 (out_11, in_3, in_2);
  nand nand_3 (out_14, in_8, in_9);
  nand nand_4 (out_12, in_5, in_4);
endmodule
