// Logisim project 7402 NOR.circ as structural Verilog: 1 circuit, main circuit main
module main (
  input  Vcc,
  input  in_2,
  input  in_3,
  input  in_4,
  input  in_5,
  input  in_6,
  input  in_7,
  input  in_8,
  input  GND,
  input  in_10,
  output out_11,
  output out_12,
  output out_13,
  output out_14
);

  nor nor_1 (out_13, in_7, in_6);
  nor nor_2 (out_11, in_2, in_3);
  nor nor_3 (out_12, in_4, in_5);
  nor nor_4 (out_14, GND, in_8);
endmodule
