// Logisim project 7404 NOT.circ as structural Verilog: 1 circuit, main circuit main
module main (
  input  in_1,
  input  in_2,
  input  in_3,
  input  in_4,
  input  in_5,
  input  in_6,
  input  in_7,
  input  in_8,
  output out_9,
  output out_10,
  output out_11,
  output out_12,
  output out_13,
  output out_14
);

  not not_1 (out_9, in_2);
  not not_2 (out_12, in_5);
  not not_3 (out_13, in_6);
  not not_4 (out_10, in_3);
  not not_5 (out_14, in_7);
  not not_6 (out_11, in_4);
endmodule
