// Logisim project 7408 AND.circ as structural Verilog: 1 circuit, main circuit main
module main (
  input  Vcc,
  input  in_2,
  input  in_3,
  input  in_4,
  input  in_5,
  input  in_6,
  input  in_7,
  input  in_8,
  input  in_9,
  input  GND,
  output out_11,
  output out_12,
  output out_13,
  output out_14
);

  and and_1 (out_11, in_3, in_2);
  and and_2 (out_13, in_6, in_7);
  and and_3 (out_14, in_8, in_9);
  and and_4 (out_12, in_5, in_4);
endmodule
