// Logisim project 74157 QUAD BIT SELECTOR.circ as structural Verilog: 1 circuit, main circuit main
module main (
  input  Vcc,
  input  G,
  input  in_3,
  input  in_4,
  input  in_5,
  input  in_6,
  input  in_7,
  input  in_8,
  input  in_9,
  input  in_10,
  input  in_11,
  input  GND,
  output out_13,
  output out_14,
  output out_15,
  output out_16
);

  wire and_1_out, and_2_out, and_3_out, and_4_out, and_5_out, and_6_out, and_7_out, and_8_out, not_1_out;

  not not_1 (not_1_out, in_7);
  and and_1 (and_1_out, not_1_out, in_8);
  and and_2 (and_2_out, in_7, in_9);
  and and_3 (and_3_out, in_4, in_7);
  or or_1 (out_13, and_3_out, and_4_out);
  and and_4 (and_4_out, in_3, not_1_out);
  or or_2 (out_15, and_1_out, and_2_out);
  and and_5 (and_5_out, not_1_out, in_10);
  or or_3 (out_16, and_5_out, and_6_out);
  and and_6 (and_6_out, in_7, in_11);
  and and_7 (and_7_out, in_6, in_7);
  or or_4 (out_14, and_7_out, and_8_out);
  and and_8 (and_8_out, in_5, not_1_out);
endmodule
