// Logisim project 74189 RAM.circ as structural Verilog: 1 circuit, main circuit main
module main (
  input  Vcc,
  input  in_2,
  input  in_3,
  input  in_4,
  input  in_5,
  input  in_6,
  input  in_7,
  input  CS,
  input  in_9,
  input  in_10,
  input  WE,
  input  in_12,
  output out_13,
  output out_14,
  output out_15,
  output out_16
);

  wire not_1_out, not_2_out, not_4_out;
  wire [3:0] controlled_buffer_2_out, ram_1_data;

  not not_1 (not_1_out, CS);
  RAM #(.addrWidth(4), .dataWidth(4), .bus("asynch")) ram_1 (
    .addr({in_4, in_3, in_2, in_7}), .data(ram_1_data), .sel(not_1_out), .ld(not_4_out));  // open: clr
  not not_2 (not_2_out, WE);
  assign ram_1_data = not_2_out ? {in_5, in_6, in_10, in_9} : 4'bz;  // Controlled_Buffer controlled_buffer_1
  assign {out_13, out_14, out_16, out_15} = ~controlled_buffer_2_out;  // NOT_Gate not_3, 4 bits wide
  assign controlled_buffer_2_out = not_4_out ? ram_1_data : 4'bz;  // Controlled_Buffer controlled_buffer_2
  not not_4 (not_4_out, not_2_out);
endmodule
