// Logisim project DIODE.circ as structural Verilog: 1 circuit, main circuit main
module main (
  input  in_1,
  output out_2
);

  assign out_2 = in_1 ? in_1 : 1'bz;  // Controlled_Buffer controlled_buffer_1
endmodule
