// Logisim project TESTING TRANSCIEVER.circ as structural Verilog: 1 circuit, main circuit main
module main (
  input  in_1,
  input  in_2,
  input  in_3,
  input  in_4,
  input  in_5,
  input  in_6,
  input  in_7,
  input  in_8,
  input  in_9,
  output out_10,
  output out_11,
  output out_12
);

  wire and_1_out, and_2_out, and_3_out, and_4_out, and_5_out, and_6_out, controlled_buffer_1_out,
       controlled_buffer_2_out, main_3_out_2, not_1_out, not_2_out, not_3_out;

  assign controlled_buffer_1_out = in_4 ? in_7 : 1'bz;  // Controlled_Buffer controlled_buffer_1
  and and_1 (and_1_out, and_4_out, in_1);
  DIODE_main main_1 (.in_1(and_2_out), .out_2(controlled_buffer_1_out));
  and and_2 (and_2_out, and_5_out, in_2);
  and and_3 (and_3_out, controlled_buffer_1_out, controlled_buffer_2_out);
  assign controlled_buffer_2_out = in_5 ? in_8 : 1'bz;  // Controlled_Buffer controlled_buffer_2
  not not_1 (not_1_out, in_4);
  assign out_10 = not_1_out ? controlled_buffer_1_out : 1'bz;  // Controlled_Buffer controlled_buffer_3
  DIODE_main main_2 (.in_1(and_1_out), .out_2(controlled_buffer_2_out));
  and and_4 (and_4_out, main_3_out_2, controlled_buffer_1_out);
  and and_5 (and_5_out, main_3_out_2, controlled_buffer_2_out);
  and and_6 (and_6_out, and_3_out, in_3);
  DIODE_main main_3 (.in_1(and_6_out), .out_2(main_3_out_2));
  assign main_3_out_2 = in_6 ? in_9 : 1'bz;  // Controlled_Buffer controlled_buffer_4
  not not_2 (not_2_out, in_5);
  assign out_11 = not_2_out ? controlled_buffer_2_out : 1'bz;  // Controlled_Buffer controlled_buffer_5
  not not_3 (not_3_out, in_6);
  assign out_12 = not_3_out ? main_3_out_2 : 1'bz;  // Controlled_Buffer controlled_buffer_6
endmodule
