// Logisim project VALIDATOR.circ as structural Verilog: 1 circuit, main circuit main
module main (
  input  [3:0] in_1,
  input  [3:0] in_2,
  input  [3:0] in_3,
  output [3:0] out_4,
  output [3:0] out_5,
  output [3:0] out_6
);

  wire not_1_out, not_2_out, not_3_out, not_4_out, not_5_out, not_6_out, not_7_out, not_8_out, not_9_out,
       not_10_out, not_11_out, not_12_out;

  assign out_6[0] = not_1_out ? in_3[0] : 1'bz;  // Controlled_Buffer controlled_buffer_1
  not not_1 (not_1_out, in_3[0]);
  assign out_6[1] = not_2_out ? in_3[1] : 1'bz;  // Controlled_Buffer controlled_buffer_2
  not not_2 (not_2_out, in_3[1]);
  assign out_6[2] = not_3_out ? in_3[2] : 1'bz;  // Controlled_Buffer controlled_buffer_3
  not not_3 (not_3_out, in_3[2]);
  assign out_6[3] = not_4_out ? in_3[3] : 1'bz;  // Controlled_Buffer controlled_buffer_4
  not not_4 (not_4_out, in_3[3]);
  assign out_5[0] = not_5_out ? in_2[0] : 1'bz;  // Controlled_Buffer controlled_buffer_5
  not not_5 (not_5_out, in_2[0]);
  assign out_5[1] = not_6_out ? in_2[1] : 1'bz;  // Controlled_Buffer controlled_buffer_6
  not not_6 (not_6_out, in_2[1]);
  assign out_5[2] = not_7_out ? in_2[2] : 1'bz;  // Controlled_Buffer controlled_buffer_7
  not not_7 (not_7_out, in_2[2]);
  assign out_5[3] = not_8_out ? in_2[3] : 1'bz;  // Controlled_Buffer controlled_buffer_8
  not not_8 (not_8_out, in_2[3]);
  assign out_4[0] = not_9_out ? in_1[0] : 1'bz;  // Controlled_Buffer controlled_buffer_9
  not not_9 (not_9_out, in_1[0]);
  assign out_4[1] = not_10_out ? in_1[1] : 1'bz;  // Controlled_Buffer controlled_buffer_10
  not not_10 (not_10_out, in_1[1]);
  assign out_4[2] = not_11_out ? in_1[2] : 1'bz;  // Controlled_Buffer controlled_buffer_11
  not not_11 (not_11_out, in_1[2]);
  assign out_4[3] = not_12_out ? in_1[3] : 1'bz;  // Controlled_Buffer controlled_buffer_12
  not not_12 (not_12_out, in_1[3]);
endmodule
