// Logisim project d flip flop test.circ as structural Verilog: 1 circuit, main circuit main
module main (
  input  in_1,
  input  in_2,
  input  in_3,
  input  in_4,
  input  in_5,
  input  in_6
);

  wire clock_1_out, controlled_buffer_1_out, controlled_buffer_3_out, nand_1_out, nand_2_out, nand_3_out,
       nand_4_out, nand_5_out, nand_6_out, nand_7_out, nand_8_out, nand_9_out, nand_10_out, nand_11_out,
       nand_12_out, nand_13_out, nand_14_out, nand_15_out, nand_16_out, not_1_out, not_2_out;

  Clock clock_1 (.out(clock_1_out));
  not not_1 (not_1_out, clock_1_out);
  nand nand_1 (nand_1_out, clock_1_out, nand_2_out);
  nand nand_2 (nand_2_out, nand_8_out, clock_1_out);
  assign controlled_buffer_1_out = in_5 ? nand_3_out : 1'bz;  // Controlled_Buffer controlled_buffer_1
  nand nand_3 (nand_3_out, nand_1_out, nand_4_out);
  nand nand_4 (nand_4_out, nand_2_out, nand_3_out);
  assign controlled_buffer_1_out = in_3 ? in_1 : 1'bz;  // Controlled_Buffer controlled_buffer_2
  nand nand_5 (nand_5_out, not_1_out, nand_6_out);
  nand nand_6 (nand_6_out, controlled_buffer_1_out, not_1_out);
  nand nand_7 (nand_7_out, nand_5_out, nand_8_out);
  nand nand_8 (nand_8_out, nand_6_out, nand_7_out);
  LED led_1 (.in(nand_8_out));
  not not_2 (not_2_out, nand_7_out);
  nand nand_9 (nand_9_out, nand_7_out, nand_10_out);
  nand nand_10 (nand_10_out, nand_16_out, nand_7_out);
  nand nand_11 (nand_11_out, nand_9_out, nand_12_out);
  nand nand_12 (nand_12_out, nand_10_out, nand_11_out);
  assign controlled_buffer_3_out = in_4 ? in_2 : 1'bz;  // Controlled_Buffer controlled_buffer_3
  assign controlled_buffer_3_out = in_6 ? nand_11_out : 1'bz;  // Controlled_Buffer controlled_buffer_4
  nand nand_13 (nand_13_out, not_2_out, nand_14_out);
  nand nand_14 (nand_14_out, controlled_buffer_3_out, not_2_out);
  nand nand_15 (nand_15_out, nand_13_out, nand_16_out);
  nand nand_16 (nand_16_out, nand_14_out, nand_15_out);
  LED led_2 (.in(nand_16_out));
endmodule
