// Logisim project testing ram.circ as structural Verilog: 1 circuit, main circuit main
module main (
  input  [3:0] in_1,
  input  _0_Write___1_Read,
  input  [3:0] in_3,
  output [3:0] out_4
);

  _74189_RAM_main main_1 (
    .in_2(in_1[1]), .in_3(in_1[2]), .out_16(out_4[1]), .in_4(in_1[3]), .in_5(in_3[3]), .out_13(out_4[3]),
    .in_7(in_1[0]), .CS(1'b0), .in_9(in_3[0]), .in_10(in_3[1]), .out_15(out_4[0]), .WE(_0_Write___1_Read),
    .in_6(in_3[2]), .out_14(out_4[2]));  // open: in_12, Vcc
endmodule
