// Logisim project testing ram2.circ as structural Verilog: 1 circuit, main circuit main
module main (
  input  [3:0] in_1,
  input  Write,
  input  Enable_Read,
  input  [3:0] in_4,
  output [3:0] out_5
);

  wire and_1_out, and_2_out, not_1_out, not_2_out;

  not not_1 (not_1_out, Write);
  not not_2 (not_2_out, Enable_Read);
  and and_1 (and_1_out, not_2_out, not_1_out);
  and and_2 (and_2_out, Enable_Read, not_1_out);
  _74189_RAM_main main_1 (
    .in_2(in_1[1]), .in_3(in_1[2]), .out_16(out_5[1]), .in_4(in_1[3]), .in_5(in_4[3]), .out_13(out_5[3]),
    .in_7(in_1[0]), .CS(and_1_out), .in_9(in_4[0]), .in_10(in_4[1]), .out_15(out_5[0]), .WE(and_2_out),
    .in_6(in_4[2]), .out_14(out_5[2]));  // open: in_12, Vcc

  // Notes on the sheet:
  //   CS
  //   WE
endmodule
