// Logisim project toggling d flip-flop.circ as structural Verilog: 1 circuit, main circuit main
module main (
  input  in_1,
  input  in_2,
  input  in_3,
  input  in_4,
  input  in_5,
  input  in_6,
  input  in_7,
  input  in_8,
  output out_9,
  output out_10,
  output out_11,
  output out_12
);

  wire clock_1_out, controlled_buffer_1_out, controlled_buffer_3_out, controlled_buffer_5_out,
       controlled_buffer_7_out, nand_1_out, nand_2_out, nand_3_out, nand_4_out, nand_5_out, nand_6_out,
       nand_8_out, nand_9_out, nand_10_out, nand_11_out, nand_12_out, nand_13_out, nand_14_out, nand_16_out,
       nand_17_out, nand_18_out, nand_19_out, nand_20_out, nand_21_out, nand_22_out, nand_24_out,
       nand_25_out, nand_26_out, nand_27_out, nand_28_out, nand_29_out, nand_30_out, nand_32_out, not_1_out,
       not_2_out, not_3_out, not_4_out, not_5_out, not_6_out, not_7_out, not_8_out, not_9_out, not_10_out,
       not_11_out, not_12_out, not_13_out, not_14_out, not_15_out, not_16_out;

  Clock clock_1 (.out(clock_1_out));
  not not_1 (not_1_out, controlled_buffer_1_out);
  not not_2 (not_2_out, clock_1_out);
  nand nand_1 (nand_1_out, controlled_buffer_1_out, clock_1_out);
  nand nand_2 (nand_2_out, clock_1_out, not_1_out);
  not not_3 (not_3_out, in_7);
  assign controlled_buffer_1_out = not_3_out ? in_3 : 1'bz;  // Controlled_Buffer controlled_buffer_1
  assign controlled_buffer_1_out = in_7 ? out_12 : 1'bz;  // Controlled_Buffer controlled_buffer_2
  nand nand_3 (nand_3_out, nand_1_out, nand_4_out);
  nand nand_4 (nand_4_out, nand_3_out, nand_2_out);
  not not_4 (not_4_out, nand_4_out);
  nand nand_5 (nand_5_out, nand_4_out, not_2_out);
  nand nand_6 (nand_6_out, not_2_out, not_4_out);
  nand nand_7 (out_12, nand_5_out, nand_8_out);
  nand nand_8 (nand_8_out, out_12, nand_6_out);
  not not_5 (not_5_out, controlled_buffer_3_out);
  not not_6 (not_6_out, out_12);
  nand nand_9 (nand_9_out, controlled_buffer_3_out, out_12);
  nand nand_10 (nand_10_out, out_12, not_5_out);
  not not_7 (not_7_out, in_8);
  assign controlled_buffer_3_out = not_7_out ? in_4 : 1'bz;  // Controlled_Buffer controlled_buffer_3
  assign controlled_buffer_3_out = in_8 ? out_11 : 1'bz;  // Controlled_Buffer controlled_buffer_4
  nand nand_11 (nand_11_out, nand_9_out, nand_12_out);
  nand nand_12 (nand_12_out, nand_11_out, nand_10_out);
  not not_8 (not_8_out, nand_12_out);
  nand nand_13 (nand_13_out, nand_12_out, not_6_out);
  nand nand_14 (nand_14_out, not_6_out, not_8_out);
  nand nand_15 (out_11, nand_13_out, nand_16_out);
  nand nand_16 (nand_16_out, out_11, nand_14_out);
  not not_9 (not_9_out, controlled_buffer_5_out);
  not not_10 (not_10_out, out_11);
  nand nand_17 (nand_17_out, controlled_buffer_5_out, out_11);
  nand nand_18 (nand_18_out, out_11, not_9_out);
  not not_11 (not_11_out, in_5);
  assign controlled_buffer_5_out = not_11_out ? in_1 : 1'bz;  // Controlled_Buffer controlled_buffer_5
  assign controlled_buffer_5_out = in_5 ? out_10 : 1'bz;  // Controlled_Buffer controlled_buffer_6
  nand nand_19 (nand_19_out, nand_17_out, nand_20_out);
  nand nand_20 (nand_20_out, nand_19_out, nand_18_out);
  not not_12 (not_12_out, nand_20_out);
  nand nand_21 (nand_21_out, nand_20_out, not_10_out);
  nand nand_22 (nand_22_out, not_10_out, not_12_out);
  nand nand_23 (out_10, nand_21_out, nand_24_out);
  nand nand_24 (nand_24_out, out_10, nand_22_out);
  not not_13 (not_13_out, controlled_buffer_7_out);
  not not_14 (not_14_out, out_10);
  nand nand_25 (nand_25_out, controlled_buffer_7_out, out_10);
  nand nand_26 (nand_26_out, out_10, not_13_out);
  not not_15 (not_15_out, in_6);
  assign controlled_buffer_7_out = not_15_out ? in_2 : 1'bz;  // Controlled_Buffer controlled_buffer_7
  assign controlled_buffer_7_out = in_6 ? out_9 : 1'bz;  // Controlled_Buffer controlled_buffer_8
  nand nand_27 (nand_27_out, nand_25_out, nand_28_out);
  nand nand_28 (nand_28_out, nand_27_out, nand_26_out);
  not not_16 (not_16_out, nand_28_out);
  nand nand_29 (nand_29_out, nand_28_out, not_14_out);
  nand nand_30 (nand_30_out, not_14_out, not_16_out);
  nand nand_31 (out_9, nand_29_out, nand_32_out);
  nand nand_32 (nand_32_out, out_9, nand_30_out);
endmodule
